// Digital circuit jelly-seven-loops.dig as structural Verilog
module jelly_seven_loops (
  input  \begin ,
  input  again,
  input  zero,
  input  mode,
  input  move,
  output out_6,
  output out_7
);

  wire d_ff_1_nq, d_ff_2_nq, nand_1_out, nand_2_out, nand_3_out, nand_4_out, nand_5_out, nand_6_out,
       nand_7_out, nand_8_out, nand_9_out, nand_10_out, nand_11_out, nand_12_out, or_1_out, or_2_out,
       or_3_out, undriven;

  nand nand_1 (nand_1_out, zero, zero);
  nand nand_2 (nand_2_out, mode, mode);
  nand nand_3 (nand_3_out, \begin , nand_1_out);
  nand nand_4 (nand_4_out, again, zero);
  nand nand_5 (nand_5_out, nand_1_out, mode);
  nand nand_6 (nand_6_out, nand_3_out, nand_3_out);
  nand nand_7 (nand_7_out, nand_4_out, nand_4_out);
  nand nand_8 (nand_8_out, nand_5_out, nand_5_out);
  nand nand_9 (nand_9_out, nand_6_out, nand_2_out);
  nand nand_10 (nand_10_out, nand_7_out, nand_2_out);
  nand nand_11 (nand_11_out, nand_9_out, nand_9_out);
  nand nand_12 (nand_12_out, nand_10_out, nand_10_out);
  or or_1 (or_1_out, nand_11_out, nand_12_out);
  or or_2 (or_2_out, or_1_out, nand_8_out);
  buf or_3 (or_3_out, undriven);  // Or open: In_1
  D_FF d_ff_1 (.D(d_ff_1_nq), .C(or_2_out), .Q(out_6), .nQ(d_ff_1_nq));
  D_FF d_ff_2 (.D(d_ff_2_nq), .C(or_3_out), .Q(out_7), .nQ(d_ff_2_nq));
endmodule
