// Digital circuit jelly-seven.dig as structural Verilog
module jelly_seven (
  input  clock,
  input  halt,
  input  D0,
  input  D1,
  input  D2,
  input  D3,
  input  D4,
  input  D5,
  input  D6,
  input  D7,
  input  MR8,
  output D0_2,
  output D1_2,
  output D2_2,
  output D3_2,
  output D4_2,
  output D5_2,
  output D6_2,
  output D7_2,
  output zero,
  output A0,
  output A1,
  output A2,
  output A3,
  output A4,
  output A5,
  output A6,
  output A7,
  output \begin ,
  output again
);

  wire and_1_out, not_1_out, pulldown_17_out, pulldown_18_out, pulldown_19_out, pulldown_20_out,
       pulldown_21_out, pulldown_22_out, pulldown_23_out, pulldown_24_out, U7_pin12, U7_pin13, U7_pin14,
       U7_pin15, U7_pin16, U7_pin17, U7_pin18, U7_pin19, u8_2_pin3, u8_2_pin6, u8_2_pin8, u8_2_pin13,
       u9_pin3, u9_pin6, U10_pin11, U10_pin12, U10_pin13, U10_pin14, U10_pin15, U10_pin16, U10_pin17,
       U10_pin18, U11_pin12, U11_pin13;
  wire [2:0] U3_p12, U5_p9, U5_p18, U11_pin14;
  wire [5:3] U8_pin11;
  wire [7:0] U6_pin12, U8_pin12;
  wire [7:3] U5_p20, U7_pin5;
  wire [7:4] U7_pin11, U12_pin7;
  wire [7:5] U4_p22;

  LED led_1 (.in(clock));
  not not_1 (not_1_out, halt);
  LED led_2 (.in(not_1_out));
  and and_1 (and_1_out, clock, not_1_out);
  LED led_3 (.in(D0_2));
  PullDown pulldown_1 (.out(D0_2));
  LED led_4 (.in(D2_2));
  LED led_5 (.in(D1_2));
  PullDown pulldown_2 (.out(D1_2));
  PullDown pulldown_3 (.out(D2_2));
  LED led_6 (.in(D4_2));
  LED led_7 (.in(D3_2));
  PullDown pulldown_4 (.out(D3_2));
  PullDown pulldown_5 (.out(D4_2));
  LED led_8 (.in(D6_2));
  LED led_9 (.in(D5_2));
  PullDown pulldown_6 (.out(D5_2));
  PullDown pulldown_7 (.out(D6_2));
  LED led_10 (.in(D7_2));
  PullDown pulldown_8 (.out(D7_2));
  _74273 U6 (
    .pin1(U11_pin14[0]), .pin2(U6_pin12[0]), .pin3(D0_2), .pin4(D1_2), .pin5(U6_pin12[1]),
    .pin6(U6_pin12[2]), .pin7(D2_2), .pin8(D3_2), .pin9(U6_pin12[3]), .pin10(1'b0), .pin11(U11_pin14[1]),
    .pin12(U6_pin12[4]), .pin13(D4_2), .pin14(D5_2), .pin15(U6_pin12[5]), .pin16(U6_pin12[6]), .pin17(D6_2),
    .pin18(D7_2), .pin19(U6_pin12[7]), .pin20(1'b1));
  _74193 U11 (
    .pin1(D1_2), .pin2(A1), .pin3(A0), .pin4(1'b0), .pin5(and_1_out), .pin6(A2), .pin7(A3), .pin8(1'b0),
    .pin9(D3_2), .pin10(D2_2), .pin11(1'b1), .pin12(U11_pin12), .pin13(U11_pin13), .pin14(U11_pin14[2]),
    .pin15(D0_2), .pin16(1'b1));
  _74193 U12 (
    .pin1(D5_2), .pin2(U12_pin7[5]), .pin3(U12_pin7[4]), .pin4(U11_pin13), .pin5(U11_pin12),
    .pin6(U12_pin7[6]), .pin7(U12_pin7[7]), .pin8(1'b0), .pin9(D7_2), .pin10(D6_2), .pin11(1'b1),
    .pin14(U11_pin14[2]), .pin15(D4_2), .pin16(1'b1));  // open: pin12, pin13
  // _28c16 U4: pin names not known; wires that end beside it: U6_pin12[7], U6_pin12[6], U6_pin12[5], U6_pin12[4], U6_pin12[3], U6_pin12[2], U6_pin12[1], U6_pin12[0], A4, A5, A6, 1'b0, 1'b1, 1'b0, 1'b0, 1'b1, 1'b0, 1'b0, 1'b0, U4_p22[7], U4_p22[6], U4_p22[5]
  _74273 U8 (
    .pin1(MR8), .pin2(U8_pin12[0]), .pin3(D0_2), .pin4(D1_2), .pin5(U8_pin12[1]), .pin6(U8_pin12[2]),
    .pin7(D2_2), .pin8(D3_2), .pin9(U8_pin12[3]), .pin10(1'b0), .pin11(U8_pin11[3]), .pin12(U8_pin12[4]),
    .pin13(D4_2), .pin14(D5_2), .pin15(U8_pin12[5]), .pin16(U8_pin12[6]), .pin17(D6_2), .pin18(D7_2),
    .pin19(U8_pin12[7]), .pin20(1'b1));
  _7432 u8_2 (
    .pin1(D0_2), .pin2(D1_2), .pin3(u8_2_pin3), .pin4(D2_2), .pin5(D3_2), .pin6(u8_2_pin6), .pin7(1'b0),
    .pin8(u8_2_pin8), .pin9(u8_2_pin6), .pin10(u8_2_pin3), .pin11(zero), .pin12(u8_2_pin8),
    .pin13(u8_2_pin13), .pin14(1'b1));
  _7432 u9 (
    .pin1(D4_2), .pin2(D5_2), .pin3(u9_pin3), .pin4(D6_2), .pin5(D7_2), .pin6(u9_pin6), .pin7(1'b0),
    .pin8(u8_2_pin13), .pin9(u9_pin6), .pin10(u9_pin3), .pin12(1'b1), .pin13(1'b1), .pin14(1'b1));  // open: pin11
  LED led_11 (.in(zero));
  LED led_12 (.in(A1));
  LED led_13 (.in(A0));
  PullDown pulldown_9 (.out(A0));
  PullDown pulldown_10 (.out(A1));
  LED led_14 (.in(A3));
  LED led_15 (.in(A2));
  PullDown pulldown_11 (.out(A2));
  PullDown pulldown_12 (.out(A3));
  LED led_16 (.in(A5));
  LED led_17 (.in(A4));
  PullDown pulldown_13 (.out(A4));
  PullDown pulldown_14 (.out(A5));
  // _28c16 U5: pin names not known; wires that end beside it: U8_pin12[7], U8_pin12[6], U8_pin12[5], U8_pin12[4], U8_pin12[3], U8_pin12[2], U8_pin12[1], U8_pin12[0], U5_p9[0], U5_p9[1], U5_p9[2], 1'b0, 1'b1, U5_p18[0], U5_p18[1], 1'b1, 1'b0, U5_p18[2], 1'b0, U5_p20[7], U5_p20[6], U5_p20[5]
  LED led_18 (.in(A7));
  LED led_19 (.in(A6));
  PullDown pulldown_15 (.out(A6));
  PullDown pulldown_16 (.out(A7));
  _74574 U9_2 (
    .pin1(U8_pin11[5]), .pin2(U5_p9[0]), .pin3(U5_p9[1]), .pin4(U5_p9[2]), .pin5(U5_p20[3]),
    .pin6(U5_p20[4]), .pin7(U5_p20[5]), .pin8(U5_p20[6]), .pin9(U5_p20[7]), .pin10(1'b0),
    .pin11(U8_pin11[4]), .pin12(D7_2), .pin13(D6_2), .pin14(D5_2), .pin15(D4_2), .pin16(D3_2), .pin17(D2_2),
    .pin18(D1_2), .pin19(D0_2), .pin20(1'b1));
  // _28c16 U1: pin names not known; wires that end beside it: A7, A6, A5, A4, A3, A2, A1, A0, U11_pin14[0], U11_pin14[1], U11_pin14[2], 1'b1, 1'b0, 1'b0, 1'b1, 1'b0, 1'b0, 1'b0, U7_pin11[7], U7_pin11[6], U7_pin11[5]
  // _28c16 U2: pin names not known; wires that end beside it: 1'b0, A7, A6, A5, A4, A3, A2, A1, A0, U5_p18[0], U5_p18[1], U5_p18[2], 1'b1, 1'b0, 1'b0, 1'b1, 1'b0, 1'b0, 1'b0, again, \begin , U8_pin11[5]
  // _28c16 U3: pin names not known; wires that end beside it: 1'b0, A7, A6, A5, A4, A3, A2, A1, A0, U3_p12[0], U3_p12[1], U3_p12[2], 1'b0, 1'b1, 1'b0, 1'b0, 1'b1, 1'b0, 1'b0, 1'b0, U7_pin5[7], U7_pin5[6], U7_pin5[5]
  _74574 U7 (
    .pin1(U7_pin11[5]), .pin2(U3_p12[0]), .pin3(U3_p12[1]), .pin4(U3_p12[2]), .pin5(U7_pin5[3]),
    .pin6(U7_pin5[4]), .pin7(U7_pin5[5]), .pin8(U7_pin5[6]), .pin9(U7_pin5[7]), .pin10(1'b0),
    .pin11(U7_pin11[4]), .pin12(U7_pin12), .pin13(U7_pin13), .pin14(U7_pin14), .pin15(U7_pin15),
    .pin16(U7_pin16), .pin17(U7_pin17), .pin18(U7_pin18), .pin19(U7_pin19), .pin20(1'b1));
  _74245 U10 (
    .pin1(U7_pin11[7]), .pin10(1'b0), .pin11(U10_pin11), .pin12(U10_pin12), .pin13(U10_pin13),
    .pin14(U10_pin14), .pin15(U10_pin15), .pin16(U10_pin16), .pin17(U10_pin17), .pin18(U10_pin18),
    .pin19(U7_pin11[6]), .pin20(1'b1));  // open: pin2, pin3, pin4, pin5, pin6, pin7, pin8, pin9
  LED led_20 (.in(pulldown_18_out));
  LED led_21 (.in(pulldown_17_out));
  PullDown pulldown_17 (.out(pulldown_17_out));
  PullDown pulldown_18 (.out(pulldown_18_out));
  LED led_22 (.in(pulldown_20_out));
  LED led_23 (.in(pulldown_19_out));
  PullDown pulldown_19 (.out(pulldown_19_out));
  PullDown pulldown_20 (.out(pulldown_20_out));
  LED led_24 (.in(pulldown_22_out));
  LED led_25 (.in(pulldown_21_out));
  PullDown pulldown_21 (.out(pulldown_21_out));
  PullDown pulldown_22 (.out(pulldown_22_out));
  LED led_26 (.in(pulldown_24_out));
  LED led_27 (.in(pulldown_23_out));
  PullDown pulldown_23 (.out(pulldown_23_out));
  PullDown pulldown_24 (.out(pulldown_24_out));

  // Notes on the sheet:
  //   Data Bus
  //   pipeline counter
  //   Zero detector
  //   opcode counter
  //   Address Bus
  //   tape control eeprom
  //   FSM Bus
  //   Decoder eeprom, translate a byte from ASCII into a valid BF instruction, ignores non valid;
  //   Code control eeprom, does  control logic of finite states for execute the current instruction;
  //   Tape control eeprom, selects which tape is active for use the Data bus and defines modes;
  //   Math operator eeprom, perform all math operations as table lookups;
  //   Basic Logic Level,
  //   check for fail states,
  //   does hold for swap tapes
  //   does hold for move direction
  //   could halt
  //   Data Bus is shared by all tapes
endmodule
